// Logisim project Q2_1.circ as structural Verilog: 1 circuit, main circuit main
module main (
  input  x,
  input  y,
  output s,
  output Q,
  output Carry_out
);

  wire and_1_out, and_2_out, clock_1_out, not_1_out, xor_1_out, xor_2_out;

  xor xor_1 (xor_1_out, x, y);
  xor xor_2 (xor_2_out, x, y);
  and and_1 (and_1_out, x, y);
  xor xor_3 (s, xor_1_out, Q);
  and and_2 (and_2_out, xor_2_out, Q);
  or or_1 (Carry_out, and_2_out, and_1_out);
  not not_1 (not_1_out, Carry_out);
  Clock clock_1 (.out(clock_1_out));
  D_Flip_Flop d_ff_1 (.clk(clock_1_out), .D(not_1_out), .Q(Q));  // open: Qn, preset, en, reset

  // Notes on the sheet:
  //   Carry in
endmodule
