// Logisim project Q3.circ as structural Verilog: 1 circuit, main circuit main
module main (
  input  x,
  input  y,
  output A,
  output z,
  output B
);

  wire and_1_out, and_2_out, and_3_out, and_4_out, and_5_out, and_6_out, and_7_out, clock_1_out, not_1_out,
       not_2_out, or_1_out, or_2_out, or_3_out;

  not not_1 (not_1_out, x);
  not not_2 (not_2_out, y);
  and and_1 (and_1_out, not_1_out, y);
  and and_2 (and_2_out, y, B);
  and and_3 (and_3_out, x, B);
  and and_4 (and_4_out, not_2_out, A);
  and and_5 (and_5_out, not_2_out, B);
  and and_6 (and_6_out, y, x);
  or or_1 (or_1_out, and_1_out, and_2_out);
  or or_2 (or_2_out, and_5_out, and_6_out);
  or or_3 (or_3_out, and_3_out, and_4_out);
  and and_7 (and_7_out, not_1_out, y);
  Clock clock_1 (.out(clock_1_out));
  or or_4 (z, and_7_out, x);
  D_Flip_Flop d_ff_1 (.clk(clock_1_out), .D(or_1_out), .Q(A));  // open: Qn, preset, en, reset
  J_K_Flip_Flop j_k_ff_1 (.J(or_2_out), .clk(clock_1_out), .K(or_3_out), .Q(B));  // open: Qn, preset, en, reset
endmodule
