// Logisim project Q4_4.circ as structural Verilog: 1 circuit, main circuit main
module main (
  output A,
  output B,
  output C
);

  wire and_1_out, and_2_out, clock_1_out, not_1_out, not_2_out, not_3_out, not_4_out, not_5_out, not_6_out,
       or_1_out, or_2_out, or_3_out, or_4_out;

  not not_1 (not_1_out, C);
  not not_2 (not_2_out, A);
  not not_3 (not_3_out, B);
  and and_1 (and_1_out, A, B);
  and and_2 (and_2_out, not_2_out, not_3_out);
  Clock clock_1 (.out(clock_1_out));
  or or_1 (or_1_out, B, not_1_out);
  or or_2 (or_2_out, C, B);
  or or_3 (or_3_out, not_1_out, not_2_out);
  or or_4 (or_4_out, and_1_out, and_2_out);
  not not_4 (not_4_out, clock_1_out);
  not not_5 (not_5_out, clock_1_out);
  not not_6 (not_6_out, clock_1_out);
  J_K_Flip_Flop j_k_ff_1 (
    .J(or_1_out), .clk(clock_1_out), .K(or_2_out), .Q(A), .en(not_4_out));  // open: Qn, preset, reset
  J_K_Flip_Flop j_k_ff_2 (
    .J(or_3_out), .clk(clock_1_out), .K(or_3_out), .Q(B), .en(not_5_out));  // open: Qn, preset, reset
  J_K_Flip_Flop j_k_ff_3 (.J(or_4_out), .clk(clock_1_out), .K(A), .Q(C), .en(not_6_out));  // open: Qn, preset, reset

  // Notes on the sheet:
  //   B
  //   A
  //   C
endmodule
